// Logisim project LastStage.circ as structural Verilog: 1 circuit, main circuit main
module main (
);

  wire and_1_out, and_2_out, or_1_out, undriven, undriven_2, undriven_3, xor_1_out, xor_2_out;

  xor xor_1 (xor_1_out, undriven_2, undriven);
  and and_1 (and_1_out, undriven_2, undriven);
  xor xor_2 (xor_2_out, xor_1_out, undriven_3);
  and and_2 (and_2_out, xor_1_out, undriven_3);
  or or_1 (or_1_out, and_2_out, and_1_out);

  // Notes on the sheet:
  //   A4
  //   B4
  //   C4
  //   F4
  //   C5
endmodule
