// Logisim project LogicDiagram.circ as structural Verilog: 1 circuit, main circuit main
module main (
  input  PR,
  input  CLR,
  input  I
);

  wire and_1_out, clock_1_out, Da_q, Db_q, not_1_out, not_2_out, not_3_out, not_4_out;

  Clock clock_1 (.out(clock_1_out));
  not not_1 (not_1_out, PR);
  not not_2 (not_2_out, CLR);
  not not_3 (not_3_out, I);
  and and_1 (and_1_out, not_3_out, Db_q);
  not not_4 (not_4_out, clock_1_out);
  D_Flip_Flop Da (.clk(clock_1_out), .D(and_1_out), .Q(Da_q), .preset(not_1_out), .reset(not_2_out));  // open: Qn, en
  D_Flip_Flop Db (.clk(not_4_out), .D(I), .Q(Db_q), .preset(not_1_out), .reset(not_2_out));  // open: Qn, en
  LED Z (.in(Da_q));
endmodule
